# Fritzing sketch hardware_schematic (saved by Fritzing 1.0.3b)

parts:
  A1 = Micro SD card reader
  S4 = Round Pushbutton
  U2 = LuaNode32 / ESP32
  S5 = Round Pushbutton
  S6 = Round Pushbutton
  S7 = Round Pushbutton

nets:
  N1: A1.Pin_1, U2.3V3
  N2: A1.Pin_2, U2.D5
  N3: A1.Pin_3, U2.D23
  N4: A1.Pin_4, U2.D19
  N5: A1.Pin_5, U2.D18
  N6: A1.Pin_6, S4.leg0, U2.GND, S5.leg0, S6.leg0, S7.leg0
  N7: S4.leg1, U2.D13
  N8: U2.D27, S6.leg1
  N9: U2.D14, S7.leg1
  N10: U2.D12, S5.leg1

custom parts:
  Micro SD card reader: Micro SD card reader.
  LuaNode32 / ESP32: ESP32 based LuaNode32
